# Fritzing sketch Heart_Rate_Schematic (saved by Fritzing 0.9.3b)
breadboards: 1

parts:
  ESP32 = ESP32S-HiLetgo [part_number=ESP32S-HiLetgo]  # not connected
  SEN11574 = Pulse Sensor [package=SIP-3]
  R1 = Resistor [tolerance=±5% resistance=220 package=THT]
  LED = LED - 5mm [color="Red (633nm)" package="5 mm [THT]"]

nets:
  N1: SEN11574.VCC, R1.Pin_1
  N2: R1.Pin_0, LED.anode

custom parts:
  ESP32S-HiLetgo: HiLetgo ESP-WROOM-32 ESP32 ESP-32S Development Board 2.4GHz Dual-Mode WiFi + Bluetooth Dual Cores Microcontroller The ESP32 integrated with Antenna switches, RF Balun, power amplifiers, low-noise amplifiers, filters, and management modules, and the entire solution occupies the least area of PCB. 2.4 GHz Wi-Fi plus Bluetooth dual-mode chip, with TSMC Ultra-low power consumption 40nm technology,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
  Pulse Sensor: Pulse Sensor Optical Heart Beat Sensor
