# Fritzing sketch Main_Schematic (saved by Fritzing 0.9.3b)
breadboards: 1

parts:
  U1 = ESP32S-HiLetgo [part_number=ESP32S-HiLetgo]
  DHT1 = DHT22 Humidity and Temperature Sensor
  DS1 = DS18B20 1-Wire Temperature Sensor Probe
  R1 = Resistor [tolerance=±5% resistance=220 package=THT]  # not connected
  Mod1 = MQ-7 breakout
  IC2 = AD8232 HeartRate Monitor [part_number=SEN-12650 chip_label=IC package="DIP (Dual Inline) [THT]"]

nets:
  N1: U1.3.3, DHT1.VDD
  N2: U1.GPIO36, IC2.OUTPUT
  N3: U1.GPIO32, Mod1.AO
  GND: U1.GND, DHT1.DATA, Mod1.GND
  N4: U1.GPIO9, IC2.LO+
  N5: U1.GPIO10, IC2.LO-
  N6: U1.GPIO15, DS1.DQ
  N7: U1.GPIO4, DHT1.GND

custom parts:
  ESP32S-HiLetgo: HiLetgo ESP-WROOM-32 ESP32 ESP-32S Development Board 2.4GHz Dual-Mode WiFi + Bluetooth Dual Cores Microcontroller The ESP32 integrated with Antenna switches, RF Balun, power amplifiers, low-noise amplifiers, filters, and management modules, and the entire solution occupies the least area of PCB. 2.4 GHz Wi-Fi plus Bluetooth dual-mode chip, with TSMC Ultra-low power consumption 40nm technology,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
  MQ-7 breakout: MQ-5 gas sensor
  AD8232 HeartRate Monitor: A DIP stand-in part for whatever IC you want. With 10 pins on a 600mil dual inline package (DIP) footprint.
